# Fritzing sketch smart-door (saved by Fritzing 0.9.9b)

parts:
  元件1 = RFID-RC522 [part_number=101218]
  元件2 = Arduino Uno (Rev3)
  J1 = Basic Servo

nets:
  N1: 元件1.SDA, 元件2.D10_PWM/SS
  N2: 元件1.SCK, 元件2.D13/SCK
  N3: 元件1.MOSI, 元件2.D11_PWM/MOSI
  N4: 元件1.MISO, 元件2.D12/MISO
  GND: 元件1.GND, 元件2.GND, J1.gnd
  N5: 元件1.RST, 元件2.D9_PWM
  3.3V: 元件1.3.3V, 元件2.3V3
  N6: 元件2.D6_PWM, J1.pulse
  5V: 元件2.5V, J1.vcc
